# Fritzing sketch TEBV_Circuit_Diagram (1) (saved by Fritzing 0.9.10b)
breadboards: 1

parts:
  Part1 = HX711 Weighing Sensor Module
  Part2 = Arduino Uno (Rev3) - ICSP
  D1 = Diode [package=diode-1n4001]
  F1 = Fan - Ventilador [package=THT]
  M1 = 1 chan 5v relay module
  VALVE1 = Plastic Solenoid Valve
  LCD1 = LCD screen
  LCM1602_IIC1 = LCM1602 IIC [part_number="LCM1602 IIC" chip_label="LCM1602 IIC" package="DIP (Dual Inline) [THT]"]
  JACK1 = 2.1mm Barrel Jack with Terminal Block

nets:
  VCC: Part1.VCC, Part2.5V, F1.5V, M1.pin_1, LCM1602_IIC1.VCC
  GND: Part1.GND, Part2.GND, F1.GND, M1.pin_2, LCM1602_IIC1.GND
  N1: Part1.DO/RX, Part2.D3_PWM
  N2: Part1.CK/TX, Part2.D2
  N3: Part2.A4/SDA, LCM1602_IIC1.SDA
  N4: Part2.A5/SCL, LCM1602_IIC1.SCL
  N5: Part2.D5_PWM, M1.pin_3
  N6: D1.A, VALVE1.no_name_yet#1, JACK1.NEG
  N7: D1.C, M1.pin_5, VALVE1.no_name_yet#2
  N8: M1.pin_6, JACK1.POS
  VSS: LCD1.VSS, LCM1602_IIC1.VSS
  VDD: LCD1.VDD, LCM1602_IIC1.VDD
  N9: LCD1.V0, LCM1602_IIC1.V0
  N10: LCD1.RS, LCM1602_IIC1.RS
  N11: LCD1.R/W, LCM1602_IIC1.RW
  N12: LCD1.E, LCM1602_IIC1.E
  N13: LCD1.DB0, LCM1602_IIC1.D0
  N14: LCD1.DB1, LCM1602_IIC1.D1
  N15: LCD1.DB2, LCM1602_IIC1.D2
  N16: LCD1.DB3, LCM1602_IIC1.D3
  N17: LCD1.DB4, LCM1602_IIC1.D4
  N18: LCD1.DB5, LCM1602_IIC1.D5
  N19: LCD1.DB6, LCM1602_IIC1.D6
  N20: LCD1.DB7, LCM1602_IIC1.D7
  N21: LCD1.LED+, LCM1602_IIC1.A
  N22: LCD1.LED-, LCM1602_IIC1.K

custom parts:
  Fan - Ventilador: Ventilador de 2 pines, se encuentra comunmente en computadoras de escritorio
  1 chan 5v relay module: 1 Channel 5V Relay Module Board Shield with Optocoupler Support High and Low Level Trigger for Arduino.
  LCM1602 IIC: I2C-Module to use a 1602 or 2004 LCD on with the wire.h libory Serial LCD Modul
